# Fritzing sketch 1 (saved by Fritzing 1.0.3b)
breadboards: 1

parts:
  LED1 = smd LED [color="Blue (525nm)" package="0603 [SMD]"]  # not connected
  HC-SR04_Sensor_1 = HC-SR04 Ultrasonic Distance Sensor
  Componente1 = Real Time Clock Module - DS1307 RTC Breakout Board
  U1 = LCD-16X2 [package=lcd-16x2_noholes]  # not connected
  Raspberry_Pi_1 = Raspberry Pi 3 [part_number=RPI-3-V1.2]
  8x8_LED_Modul_mit_MAX1 = 8x8 LED Modul mit MAX7219 [package=THT]  # not connected
  DHT1 = DHT11 Humitidy and Temperature Sensor (3 pins)  # not connected
  R1 = Resistor [tolerance=±5% resistance=330 package="1206 [SMD]"]  # not connected
  Keypad4x1 = Keypad Membran 4x4  # not connected
  VCC1 = Battery [internal_resistance=0.1Ω]

nets:
  N1: HC-SR04_Sensor_1.VCC, VCC1.-
  N2: Componente1.SQW, Raspberry_Pi_1.GPIO8
  N3: Componente1.SCL, Raspberry_Pi_1.GPIO25
  N4: Componente1.SDA, Raspberry_Pi_1.GND

custom parts:
  DHT11 Humitidy and Temperature Sensor (3 pins): DHT11 Humidity and Temperature Sensor (3 pins).
  Keypad Membran 4x4: Membrane Keypad 4x4 Matrix
